// Logisim project B1-Group1-Software-Simulation.circ as structural Verilog: 1 circuit, main circuit main
module main (
  input  s2,
  input  s1,
  input  s0,
  input  a4,
  input  a3,
  input  a2,
  input  a1,
  input  b4,
  input  b3,
  input  b2,
  input  b1
);

  wire n7408_1_pin2, n7408_1_pin3, n7408_1_pin5, n7408_1_pin6, n7408_1_pin8, n7408_1_pin9, n7408_1_pin11,
       n7408_1_pin12, n7408_2_pin2, n7408_2_pin8, n7408_2_pin11, n7408_3_pin1, n7408_3_pin6, n7408_3_pin9,
       n7408_3_pin11, n7408_3_pin12, n7408_4_pin1, n7408_4_pin2, n7408_4_pin3, n7408_4_pin5, n7408_4_pin6,
       n7408_4_pin8, n7408_4_pin9, n7408_4_pin11, n7432_1_pin1, n7486_1_pin3, n74283_1_pin1, n74283_1_pin2,
       n74283_1_pin4, n74283_1_pin6, n74283_1_pin7, n74283_1_pin9, n74283_1_pin10, n74283_1_pin11,
       n74283_1_pin14, n74283_1_pin15, n74283_2_pin2, n74283_2_pin4, n74283_2_pin10, n74283_2_pin14;

  LED cout (.in(n7408_4_pin11));
  _7408 u_7408_1 (
    .pin1(a4), .pin2(n7408_1_pin2), .pin3(n7408_1_pin3), .pin4(a1), .pin5(n7408_1_pin5), .pin6(n7408_1_pin6),
    .pin13(a3), .pin12(n7408_1_pin12), .pin11(n7408_1_pin11), .pin10(a2), .pin9(n7408_1_pin9),
    .pin8(n7408_1_pin8));
  LED sum4 (.in(n74283_1_pin10));
  _74283 u_74283_1 (
    .pin1(n74283_1_pin1), .pin2(n74283_1_pin2), .pin3(n74283_1_pin2), .pin4(n74283_1_pin4),
    .pin5(n7408_1_pin11), .pin6(n74283_1_pin6), .pin7(n74283_1_pin7), .pin15(n74283_1_pin15),
    .pin14(n74283_1_pin14), .pin12(n7408_1_pin3), .pin11(n74283_1_pin11), .pin10(n74283_1_pin10),
    .pin9(n74283_1_pin9));  // open: pin13
  LED sum3 (.in(n74283_1_pin4));
  _7408 u_7408_2 (
    .pin1(b3), .pin2(n7408_2_pin2), .pin3(n74283_1_pin6), .pin4(b4), .pin5(n7408_2_pin2),
    .pin6(n74283_1_pin11), .pin13(n7408_2_pin2), .pin12(b2), .pin11(n7408_2_pin11), .pin10(n7408_2_pin2),
    .pin9(b1), .pin8(n7408_2_pin8));
  _7408 u_7408_3 (
    .pin1(n7408_3_pin1), .pin2(n74283_1_pin1), .pin3(n74283_1_pin15), .pin4(n7408_3_pin1), .pin5(s0),
    .pin6(n7408_3_pin6), .pin13(n7408_3_pin1), .pin12(n7408_3_pin12), .pin11(n7408_3_pin11),
    .pin10(n7408_3_pin1), .pin9(n7408_3_pin9), .pin8(n74283_1_pin7));
  LED sum2 (.in(n74283_2_pin10));
  LED sum1 (.in(n74283_2_pin4));
  _74283 u_74283_2 (
    .pin1(n7408_3_pin12), .pin2(n74283_2_pin2), .pin3(n74283_2_pin2), .pin4(n74283_2_pin4),
    .pin5(n7408_1_pin6), .pin6(n7408_2_pin8), .pin7(n7408_3_pin6), .pin15(n7408_3_pin11),
    .pin14(n74283_2_pin14), .pin12(n7408_1_pin8), .pin11(n7408_2_pin11), .pin10(n74283_2_pin10),
    .pin9(n7408_3_pin9));  // open: pin13
  _7432 u_7432_1 (
    .pin1(n7432_1_pin1), .pin2(b1), .pin3(n7408_1_pin5), .pin4(n7432_1_pin1), .pin5(b2), .pin6(n7408_1_pin9),
    .pin13(n7432_1_pin1), .pin12(b3), .pin11(n7408_1_pin12), .pin10(n7432_1_pin1), .pin9(b4),
    .pin8(n7408_1_pin2));
  _7432 u_7432_2 (
    .pin1(n7408_3_pin1), .pin2(s2), .pin3(n7432_1_pin1));  // open: pin4, pin5, pin6, pin13, pin12, pin11, pin10, pin9, pin8
  _7408 u_7408_4 (
    .pin1(n7408_4_pin1), .pin2(n7408_4_pin2), .pin3(n7408_4_pin3), .pin4(n7408_4_pin3), .pin5(n7408_4_pin5),
    .pin6(n7408_4_pin6), .pin13(n74283_1_pin9), .pin12(n7408_3_pin1), .pin11(n7408_4_pin11),
    .pin10(n7408_4_pin6), .pin9(n7408_4_pin9), .pin8(n7408_4_pin8));
  _7486 u_7486_1 (
    .pin1(n74283_1_pin9), .pin2(n74283_1_pin15), .pin3(n7486_1_pin3), .pin13(n7408_3_pin1), .pin12(s2),
    .pin11(n7408_2_pin2));  // open: pin4, pin5, pin6, pin10, pin9, pin8
  _7404 u_7404_1 (
    .pin1(s1), .pin2(n7408_3_pin1), .pin3(n74283_2_pin4), .pin4(n7408_4_pin1), .pin5(n74283_2_pin10),
    .pin6(n7408_4_pin2), .pin11(n74283_1_pin10), .pin10(n7408_4_pin5), .pin9(n74283_1_pin4),
    .pin8(n7408_4_pin9));  // open: pin13, pin12
  LED Z_flag (.in(n7408_4_pin8));
  LED V_flag (.in(n7486_1_pin3));
  LED C_flag (.in(n7408_4_pin11));
  LED S_flag (.in(n74283_1_pin10));
  // also tied to GND on the sheet: {n74283_1_pin2, n74283_2_pin2}
  // also tied to VCC on the sheet: {n74283_1_pin14, n74283_2_pin14}

  // Notes on the sheet:
  //   x4
  //   x1
  //   x3
  //   x2
  //   y4
  //   z4
  //   y3
  //   z1
  //   y2
  //   z3
  //   s2+s1'
  //   s2 xor s1'
  //   y1 = b1(s2 xor s1')
  //   c1 = s1' and s0
  //   z2
endmodule
