// Logisim project FPA_B1_Group1-1.circ as structural Verilog: 10 circuits, main circuit difference
// normalize
module main (
  input  sign,
  input  [9:0] in_2,
  input  [20:0] in_3,
  input  sign_2,
  input  [9:0] in_5,
  input  [20:0] in_6,
  output overflw,
  output underflw,
  output sign_3,
  output [9:0] out_10,
  output [20:0] out_11,
  output [31:0] out_12,
  output [31:0] out_13,
  output [31:0] out_14,
  output [31:0] out_15,
  output [4:0] out_16,
  output [4:0] shift_amount,
  output [10:0] out_18
);

  wire comparator_1_eq, comparator_1_gt, comparator_2_eq, comparator_2_gt, difference_1_e2___e1,
       larger_fraction_selector_1_sign_out, larger_fraction_selector_2_sign_out, n7404_1_p2,
       normalize_1_all_zeros;
  wire [4:0] n21_checker_1__5bit_shamt;
  wire [9:0] difference_1_e1_e2, larger_exp_selector_1_larger_exp;
  wire [10:0] exp_shift_amnt_1__11bit_exp_out;
  wire [20:0] larger_fraction_selector_1_output, larger_fraction_selector_2_output;
  wire [21:0] shifter_1_out;
  wire [30:0] big_alu_1_output;

  difference difference_1 (.exp_2(in_5), .exp_1(in_2), .E2___E1(difference_1_e2___e1), .E1_E2(difference_1_e1_e2));
  Larger_Exp_Selector larger_exp_selector_1 (
    .selector(difference_1_e2___e1), .exp_1(in_2), .exp_2(in_5), .larger_exp(larger_exp_selector_1_larger_exp));
  // _7404 7404_1: pin names not known; wires that end beside it: difference_1_e2___e1, n7404_1_p2, 1'b0, 1'b1
  _21_checker u_21_checker_1 (._10_bit_exp(difference_1_e1_e2), ._5bit_shamt(n21_checker_1__5bit_shamt));
  Larger_Fraction_Selector larger_fraction_selector_1 (
    .selector(difference_1_e2___e1), .sign_1(sign), .frac_1(in_3), .sign_2(sign_2), .frac_2(in_6),
    .sign_out(larger_fraction_selector_1_sign_out), .\output (larger_fraction_selector_1_output));
  Larger_Fraction_Selector larger_fraction_selector_2 (
    .selector(n7404_1_p2), .sign_1(sign), .frac_1(in_3), .sign_2(sign_2), .frac_2(in_6),
    .sign_out(larger_fraction_selector_2_sign_out), .\output (larger_fraction_selector_2_output));
  exp_shift_amnt exp_shift_amnt_1 (
    ._11bit_exp({1'b0, larger_exp_selector_1_larger_exp}), ._5bit_shift_amnt(out_16),
    ._11bit_exp_out(exp_shift_amnt_1__11bit_exp_out));  // open: carry_out
  Shifter #(.width(22), .shift("lr")) shifter_1 (
    .in({1'b1, larger_fraction_selector_2_output}), .\dist (n21_checker_1__5bit_shamt), .out(shifter_1_out));
  big_ALU big_alu_1 (
    .\output ({sign_3, big_alu_1_output}), .frac_1({1'b1, larger_fraction_selector_1_output}),
    .sign_1(larger_fraction_selector_1_sign_out), .sign_2(larger_fraction_selector_2_sign_out),
    .frac_2(shifter_1_out));
  _2_s_complement_32bit u_2_s_complement_32bit_1 (
    ._32bit_output(out_14), .sign(sign_3), ._32bit_input({sign_3, big_alu_1_output}));
  exp_shift_amnt exp_shift_amnt_2 (
    ._11bit_exp(exp_shift_amnt_1__11bit_exp_out), ._5bit_shift_amnt(shift_amount),
    ._11bit_exp_out({out_18[10], out_10}));  // open: carry_out
  normalize normalize_1 (
    ._32_bit_input(out_14), ._32_bit_output(out_15), .shift_amount(out_16), .all_zeros(normalize_1_all_zeros));  // open: out_2
  Comparator #(.width(11)) comparator_1 (
    .a({out_18[10], out_10}), .b(11'h3ff), .gt(comparator_1_gt), .eq(comparator_1_eq));  // open: lt
  Comparator #(.width(11)) comparator_2 (
    .a({11{1'b0}}), .b({out_18[10], out_10}), .gt(comparator_2_gt), .eq(comparator_2_eq));  // open: lt
  rounding rounding_1 (.normalized_input(out_15), ._23_bit_significant_in_the_LSB(out_12));
  // _7432 7432_1: pin names not known; wires that end beside it: comparator_1_gt, comparator_1_eq, overflw, comparator_2_gt, comparator_2_eq, underflw
  normalize normalize_2 (
    ._32_bit_input(out_12), ._32_bit_output({out_13[31], out_11, out_13[9:0]}), .shift_amount(shift_amount));  // open: out_2, all_zeros

  assign out_13[30:10] = out_11;
  assign out_18[9:0] = out_10;

  // Notes on the sheet:
  //   10bit exp
  //   exp-diffrenece
  //   A
  //   21 bit frac
  //   E2>E1 ?
  //   |e1-e2|
  //   L-exp
  //   >21 modifier
  //   B
  //   10 bit exp
  //   21 bit frac
  //   largerE-frac
  //   smallerE-frac
  //   exp>=0
  //   10 bit exp
  //   exp+shift
  //   A+B
  //   21 bit frac
  //   frac-sign
  //   2's
  //   frac-adder
  //   exp+shift
  //   normalize
  //   if exp>=1023overflw
  //   shift amount
  //   exp-result
  //   if exp<=0 underflw
  //   rounding
  //   21 bit frac
  //   normalize
endmodule

module difference (
  input  [9:0] exp_2,
  input  [9:0] exp_1,
  output E2___E1,
  output [9:0] E1_E2
);

  wire [31:0] bit_extender_1_out, bit_extender_2_out, subtractor_1_out;
  wire [31:10] n2_s_complement_32bit_1__32bit_output;

  assign bit_extender_1_out = {{22{1'b0}}, exp_1};  // Bit_Extender bit_extender_1
  Subtractor #(.width(32)) subtractor_1 (
    .a(bit_extender_1_out), .b(bit_extender_2_out), .out(subtractor_1_out), .bin(1'b0), .bout(E2___E1));
  assign bit_extender_2_out = {{22{1'b0}}, exp_2};  // Bit_Extender bit_extender_2
  _2_s_complement_32bit u_2_s_complement_32bit_1 (
    ._32bit_output({n2_s_complement_32bit_1__32bit_output, E1_E2}), .sign(E2___E1),
    ._32bit_input(subtractor_1_out));

  // Notes on the sheet:
  //   32 bit 2's complementer
endmodule

module Larger_Exp_Selector (
  input  [9:0] exp_1,
  input  [9:0] exp_2,
  input  selector,
  output [9:0] larger_exp
);

  // _74157 74157_1: pin names not known; wires that end beside it: 1'b1, selector, 1'b0, exp_1[3], exp_1[1], exp_2[3], exp_2[1], larger_exp[3], larger_exp[1], exp_1[2], exp_1[0], exp_2[2], exp_2[0], larger_exp[2], larger_exp[0], 1'b0
  // _74157 74157_2: pin names not known; wires that end beside it: 1'b1, selector, 1'b0, exp_1[6], exp_1[4], exp_2[6], exp_2[4], larger_exp[6], larger_exp[4], exp_1[7], exp_1[5], exp_2[7], exp_2[5], larger_exp[7], larger_exp[5], 1'b0
  // _74157 74157_3: pin names not known; wires that end beside it: 1'b1, selector, 1'b0, exp_1[8], exp_2[8], larger_exp[8], exp_1[9], exp_2[9], larger_exp[9], 1'b0
endmodule

module Larger_Fraction_Selector (
  input  selector,
  input  sign_1,
  input  [20:0] frac_1,
  input  sign_2,
  input  [20:0] frac_2,
  output sign_out,
  output [20:0] \output 
);

  // _74157 74157_1: pin names not known; wires that end beside it: 1'b1, selector, 1'b0, frac_1[2], frac_1[0], frac_2[2], frac_2[0], \output [2], \output [0], frac_1[3], frac_1[1], frac_2[3], frac_2[1], \output [3], \output [1], 1'b0
  // _74157 74157_2: pin names not known; wires that end beside it: 1'b1, selector, 1'b0, frac_1[5], frac_1[4], frac_2[5], frac_2[4], \output [5], \output [4], frac_1[6], frac_2[6], \output [6], 1'b0
  // _74157 74157_3: pin names not known; wires that end beside it: 1'b1, selector, 1'b0, frac_1[9], frac_1[8], frac_2[9], frac_2[8], \output [9], \output [8], frac_1[10], frac_1[7], frac_2[10], frac_2[7], \output [10], \output [7], 1'b0
  // _74157 74157_4: pin names not known; wires that end beside it: 1'b1, selector, 1'b0, frac_1[13], frac_1[11], frac_2[13], frac_2[11], \output [13], \output [11], frac_1[14], frac_1[12], frac_2[14], frac_2[12], \output [14], \output [12], 1'b0
  // _74157 74157_5: pin names not known; wires that end beside it: 1'b1, selector, 1'b0, frac_1[17], frac_1[15], frac_2[17], frac_2[15], \output [17], \output [15], frac_1[18], frac_1[16], frac_2[18], frac_2[16], \output [18], \output [16], 1'b0
  // _74157 74157_6: pin names not known; wires that end beside it: 1'b1, selector, 1'b0, sign_1, frac_1[19], sign_2, frac_2[19], sign_out, \output [19], frac_1[20], frac_2[20], \output [20], 1'b0

  // Notes on the sheet:
  //   if 0 select frac-1
  //   fraction which has larger exponent
  //   14
endmodule

module _21_checker (
  input  [9:0] _10_bit_exp,
  output [4:0] _5bit_shamt
);

  wire n7432_1_p3, n7432_1_p6, n7432_1_p11, n7432_1_p14;

  // _7432 7432_1: pin names not known; wires that end beside it: _10_bit_exp[9], _10_bit_exp[8], n7432_1_p3, n7432_1_p3, _10_bit_exp[7], n7432_1_p6, 1'b0, 1'b1, n7432_1_p6, _10_bit_exp[6], n7432_1_p11, n7432_1_p11, _10_bit_exp[5], n7432_1_p14
  // _7432 7432_2: pin names not known; wires that end beside it: _10_bit_exp[2], n7432_1_p14, _5bit_shamt[2], n7432_1_p14, _10_bit_exp[1], _5bit_shamt[1], 1'b0, 1'b1, _10_bit_exp[4], n7432_1_p14, _5bit_shamt[4], n7432_1_p14, _10_bit_exp[3], _5bit_shamt[3]
  // _7432 7432_3: pin names not known; wires that end beside it: 1'b0, 1'b1, _10_bit_exp[0], n7432_1_p14, _5bit_shamt[0]

  // Notes on the sheet:
  //   before this modification shift amount could be 1023, now we changed the upper limit to 31
endmodule

module big_ALU (
  input  [21:0] frac_2,
  input  [21:0] frac_1,
  input  sign_1,
  input  sign_2,
  output [31:0] \output 
);

  wire [31:0] adder_1_out, bit_extender_2_out, n7486_1_p8, n7486_1_p9, n7486_9_p9;

  // _7486 7486_1: pin names not known; wires that end beside it: n7486_1_p8[31], sign_1, n7486_1_p9[31], sign_1, n7486_1_p8[30], 1'b1, sign_1, n7486_1_p8[0], n7486_1_p9[0], sign_1
  // _7486 7486_2: pin names not known; wires that end beside it: n7486_1_p9[30], 1'b0, n7486_1_p8[29], sign_1, n7486_1_p9[29], sign_1, n7486_1_p8[28], n7486_1_p8[1], n7486_1_p9[1], 1'b1, sign_1, n7486_1_p8[2], n7486_1_p9[2], sign_1
  // _7486 7486_3: pin names not known; wires that end beside it: n7486_1_p9[28], 1'b0, n7486_1_p8[27], sign_1, n7486_1_p9[27], sign_1, n7486_1_p8[26], n7486_1_p8[3], n7486_1_p9[3], 1'b1, sign_1, n7486_1_p8[4], n7486_1_p9[4], sign_1
  // _7486 7486_4: pin names not known; wires that end beside it: n7486_1_p9[26], 1'b0, n7486_1_p8[25], sign_1, n7486_1_p9[25], sign_1, n7486_1_p8[24], n7486_1_p8[5], n7486_1_p9[5], 1'b1, n7486_1_p8[6], sign_1, n7486_1_p9[6], sign_1
  // _7486 7486_5: pin names not known; wires that end beside it: n7486_1_p9[24], 1'b0, n7486_1_p8[23], sign_1, n7486_1_p9[23], sign_1, n7486_1_p8[22], n7486_1_p8[7], n7486_1_p9[7], 1'b1, n7486_1_p8[8], sign_1, n7486_1_p9[8], sign_1
  // _7486 7486_6: pin names not known; wires that end beside it: n7486_1_p9[22], 1'b0, n7486_1_p8[21], sign_1, n7486_1_p9[21], sign_1, n7486_1_p8[20], n7486_1_p8[9], n7486_1_p9[9], 1'b1, n7486_1_p8[10], sign_1, n7486_1_p9[10], sign_1
  // _7486 7486_7: pin names not known; wires that end beside it: n7486_1_p9[20], 1'b0, n7486_1_p8[19], sign_1, n7486_1_p9[19], sign_1, n7486_1_p8[18], n7486_1_p8[11], n7486_1_p9[11], 1'b1, n7486_1_p8[12], sign_1, n7486_1_p9[12], sign_1
  // _7486 7486_8: pin names not known; wires that end beside it: n7486_1_p9[18], 1'b0, n7486_1_p8[17], sign_1, n7486_1_p9[17], sign_1, n7486_1_p8[16], n7486_1_p9[16], 1'b0, n7486_1_p8[13], n7486_1_p9[13], 1'b1, n7486_1_p8[14], sign_1, n7486_1_p9[14], sign_1, n7486_1_p8[15], n7486_1_p9[15]
  assign n7486_1_p8 = {{10{1'b0}}, frac_1};  // Bit_Extender bit_extender_1
  Adder #(.width(32)) adder_1 (.a(n7486_1_p9), .b({32{1'b0}}), .out(adder_1_out), .cin(sign_1));  // open: cout
  assign bit_extender_2_out = {{10{1'b0}}, frac_2};  // Bit_Extender bit_extender_2
  // _7486 7486_9: pin names not known; wires that end beside it: bit_extender_2_out[31], sign_2, n7486_9_p9[31], sign_2, bit_extender_2_out[30], 1'b1, sign_2, bit_extender_2_out[0], n7486_9_p9[0], sign_2
  // _7486 7486_10: pin names not known; wires that end beside it: n7486_9_p9[30], 1'b0, bit_extender_2_out[29], sign_2, n7486_9_p9[29], sign_2, bit_extender_2_out[28], bit_extender_2_out[1], n7486_9_p9[1], 1'b1, sign_2, bit_extender_2_out[2], n7486_9_p9[2], sign_2
  // _7486 7486_11: pin names not known; wires that end beside it: n7486_9_p9[28], 1'b0, bit_extender_2_out[27], sign_2, n7486_9_p9[27], sign_2, bit_extender_2_out[26], bit_extender_2_out[3], n7486_9_p9[3], 1'b1, sign_2, bit_extender_2_out[4], n7486_9_p9[4], sign_2
  // _7486 7486_12: pin names not known; wires that end beside it: n7486_9_p9[26], 1'b0, bit_extender_2_out[25], sign_2, n7486_9_p9[25], sign_2, bit_extender_2_out[24], bit_extender_2_out[5], n7486_9_p9[5], 1'b1, bit_extender_2_out[6], sign_2, n7486_9_p9[6], sign_2
  // _7486 7486_13: pin names not known; wires that end beside it: n7486_9_p9[24], 1'b0, bit_extender_2_out[23], sign_2, n7486_9_p9[23], sign_2, bit_extender_2_out[22], bit_extender_2_out[7], n7486_9_p9[7], 1'b1, bit_extender_2_out[8], sign_2, n7486_9_p9[8], sign_2
  // _7486 7486_14: pin names not known; wires that end beside it: n7486_9_p9[22], 1'b0, bit_extender_2_out[21], sign_2, n7486_9_p9[21], sign_2, bit_extender_2_out[20], bit_extender_2_out[9], n7486_9_p9[9], 1'b1, bit_extender_2_out[10], sign_2, n7486_9_p9[10], sign_2
  // _7486 7486_15: pin names not known; wires that end beside it: n7486_9_p9[20], 1'b0, bit_extender_2_out[19], sign_2, n7486_9_p9[19], sign_2, bit_extender_2_out[18], bit_extender_2_out[11], n7486_9_p9[11], 1'b1, bit_extender_2_out[12], sign_2, n7486_9_p9[12], sign_2
  // _7486 7486_16: pin names not known; wires that end beside it: n7486_9_p9[18], 1'b0, bit_extender_2_out[17], sign_2, n7486_9_p9[17], sign_2, bit_extender_2_out[16], n7486_9_p9[16], 1'b0, bit_extender_2_out[13], n7486_9_p9[13], 1'b1, bit_extender_2_out[14], sign_2, n7486_9_p9[14], sign_2, bit_extender_2_out[15], n7486_9_p9[15]
  Adder #(.width(32)) adder_2 (.a(n7486_9_p9), .b(adder_1_out), .out(\output ), .cin(sign_2));  // open: cout
endmodule

module _2_s_complement_32bit (
  input  [31:0] _32bit_input,
  input  sign,
  output [31:0] _32bit_output
);

  wire [31:0] n7486_8_p14;

  // _7486 7486_1: pin names not known; wires that end beside it: _32bit_input[16], sign, n7486_8_p14[16], _32bit_input[17], sign, n7486_8_p14[17], 1'b1, _32bit_input[15], sign, n7486_8_p14[15], _32bit_input[14], sign
  // _7486 7486_2: pin names not known; wires that end beside it: 1'b0, _32bit_input[18], sign, n7486_8_p14[18], _32bit_input[19], sign, n7486_8_p14[19], n7486_8_p14[14], 1'b1, _32bit_input[13], sign, n7486_8_p14[13], _32bit_input[12], sign
  // _7486 7486_3: pin names not known; wires that end beside it: 1'b0, _32bit_input[20], sign, n7486_8_p14[20], _32bit_input[21], sign, n7486_8_p14[21], 1'b0, n7486_8_p14[12], 1'b1, _32bit_input[11], sign, n7486_8_p14[11], sign, _32bit_input[10], n7486_8_p14[10]
  // _7486 7486_4: pin names not known; wires that end beside it: _32bit_input[22], sign, n7486_8_p14[22], _32bit_input[23], sign, n7486_8_p14[23], 1'b1, _32bit_input[9], sign, n7486_8_p14[9], _32bit_input[8], sign
  // _7486 7486_5: pin names not known; wires that end beside it: 1'b0, _32bit_input[24], sign, n7486_8_p14[24], _32bit_input[25], sign, n7486_8_p14[25], n7486_8_p14[8], 1'b1, _32bit_input[7], sign, n7486_8_p14[7], sign, _32bit_input[6]
  // _7486 7486_6: pin names not known; wires that end beside it: 1'b0, _32bit_input[26], sign, n7486_8_p14[26], _32bit_input[27], sign, n7486_8_p14[27], n7486_8_p14[6], 1'b1, _32bit_input[5], sign, n7486_8_p14[5], sign, _32bit_input[4]
  // _7486 7486_7: pin names not known; wires that end beside it: 1'b0, _32bit_input[28], sign, n7486_8_p14[28], sign, _32bit_input[29], n7486_8_p14[29], 1'b0, n7486_8_p14[4], 1'b1, _32bit_input[3], sign, n7486_8_p14[3], sign, _32bit_input[2], n7486_8_p14[2]
  // _7486 7486_8: pin names not known; wires that end beside it: _32bit_input[30], sign, n7486_8_p14[30], sign, _32bit_input[31], n7486_8_p14[31], 1'b0, 1'b1, _32bit_input[1], sign, n7486_8_p14[1], sign, _32bit_input[0], n7486_8_p14[0]
  Adder #(.width(32)) adder_1 (.a(n7486_8_p14), .b({32{1'b0}}), .out(_32bit_output), .cin(sign));  // open: cout
endmodule

module rounding (
  input  [31:0] normalized_input,
  output [31:0] _23_bit_significant_in_the_LSB
);

  wire adder_1_cout, n7404_1_p1, n7404_1_p3, n7404_1_p5, n7408_1_p3, n7408_1_p6, n7408_1_p8, n7408_1_p9,
       n7408_1_p12, n7432_1_p3, n7432_1_p6, n7432_1_p9, n7432_1_p12, n7432_2_p3, n7432_2_p6, n7432_2_p9,
       n7432_3_p7;

  // _7432 7432_1: pin names not known; wires that end beside it: normalized_input[0], normalized_input[1], n7432_1_p3, n7432_1_p3, normalized_input[2], n7432_1_p6, n7432_1_p6, normalized_input[3], n7432_1_p9, n7432_1_p9, normalized_input[4], n7432_1_p12
  // _7432 7432_2: pin names not known; wires that end beside it: n7432_1_p12, normalized_input[5], n7432_2_p3, n7432_2_p3, normalized_input[6], n7432_2_p6, n7432_2_p6, normalized_input[7], n7432_2_p9
  // _7404 7404_1: pin names not known; wires that end beside it: n7404_1_p1, n7432_2_p9, n7404_1_p3, normalized_input[8], n7404_1_p5, normalized_input[9], n7404_1_p1
  Adder #(.width(32)) adder_1 (
    .a({{10{1'b0}}, normalized_input[31:10]}), .b({32{1'b0}}), .out(_23_bit_significant_in_the_LSB),
    .cin(n7432_3_p7), .cout(adder_1_cout));
  // _7408 7408_1: pin names not known; wires that end beside it: normalized_input[9], n7404_1_p5, n7408_1_p3, n7408_1_p3, n7404_1_p3, n7408_1_p6, normalized_input[9], n7408_1_p8, n7408_1_p9, n7408_1_p6, normalized_input[10], n7408_1_p12
  // _7432 7432_3: pin names not known; wires that end beside it: adder_1_cout, n7432_2_p9, normalized_input[8], n7408_1_p8, n7408_1_p12, n7408_1_p9, n7432_3_p7

  // Notes on the sheet:
  //   21bit frac ,G,R,S
  //   22 bit from MSB is our significant
  //   we shifted it 22 bit of LSB
  //   Don't worry, the result will be normalized
  //   R
  //   G
  //   S
  //   S'
  //   S
  //   R'
  //   GR'S'
  //   r+S
  //   carry in
  //   32 bit adder
  //   G(r+S)
  //   G(R+S)
  //   0th bit / LSB of 22 bit significant
  //   if( G(R+S) or (GR'S'&0 th bit is 1)
  //   GR'S'&odd
  //   add-1
  //   else add 0
endmodule

module exp_shift_amnt (
  input  [4:0] _5bit_shift_amnt,
  input  [10:0] _11bit_exp,
  output [10:0] _11bit_exp_out,
  output carry_out
);

  wire comparator_1_eq, comparator_1_gt, n7432_1_p3;
  wire [4:0] n74157_1_p4;
  wire [31:0] adder_1_out, bit_extender_1_out, bit_extender_2_out, bit_extender_3_out;
  wire [31:11] subtractor_1_out;

  assign bit_extender_1_out = {{21{1'b0}}, _11bit_exp};  // Bit_Extender bit_extender_1
  assign bit_extender_2_out = {{27{1'b0}}, n74157_1_p4};  // Bit_Extender bit_extender_2
  Adder #(.width(32)) adder_1 (.a(bit_extender_1_out), .b(bit_extender_2_out), .out(adder_1_out));  // open: cin, cout
  assign bit_extender_3_out = {{27{1'b0}}, _5bit_shift_amnt};  // Bit_Extender bit_extender_3
  Comparator #(.width(6)) comparator_1 (
    .a({1'b0, _5bit_shift_amnt}), .b(6'b001001), .gt(comparator_1_gt), .eq(comparator_1_eq));  // open: lt
  // _7432 7432_1: pin names not known; wires that end beside it: comparator_1_gt, comparator_1_eq, n7432_1_p3
  // _74157 74157_1: pin names not known; wires that end beside it: n7432_1_p3, _5bit_shift_amnt[0], 1'b0, n74157_1_p4[0], _5bit_shift_amnt[1], 1'b1, n74157_1_p4[1], 1'b0, _5bit_shift_amnt[2], 1'b0, n74157_1_p4[2], _5bit_shift_amnt[3], 1'b1, n74157_1_p4[3]
  // _74157 74157_2: pin names not known; wires that end beside it: n7432_1_p3, _5bit_shift_amnt[4], 1'b0, n74157_1_p4[4], 1'b0
  Subtractor #(.width(32)) subtractor_1 (
    .a(adder_1_out), .b(bit_extender_3_out), .out({subtractor_1_out, _11bit_exp_out}), .bin(1'b0),
    .bout(carry_out));

  // Notes on the sheet:
  //   making it unsigned
  //   if shiftamnt >=9 then we need to add xtra 10
  //   else keep the const as the shift amnt
  //   it is actually possible for the shamt to be 0 when our significant contains all 0
  //   & shamt>=9 when there is atleast one 1 in the 23 bit from LSB (before normalization there is 23 bit significant) 
  //   9,10,111
  //   (10-shift amnt)
  //   10-9=1
  //   exp+diff
  //   shift amnt=10 mane 1.0000
  //   10-10=0+exp=exp
  //   11->0.167899
  //   4+1=5
  //   10-11=-1+exp
  //   1.67*10-1
  //   so it's not pssible shamt to be in between 1 to 8
endmodule

module normalize (
  input  [31:0] _32_bit_input,
  output [31:0] out_2,
  output [31:0] _32_bit_output,
  output [4:0] shift_amount,
  output all_zeros
);

  wire bitfinder_1_found;

  BitFinder #(.width(32)) bitfinder_1 (
    .in({_32_bit_input[0], _32_bit_input[1], _32_bit_input[2], _32_bit_input[3], _32_bit_input[4], _32_bit_input[5], _32_bit_input[6], _32_bit_input[7], _32_bit_input[8], _32_bit_input[9], _32_bit_input[10], _32_bit_input[11], _32_bit_input[12], _32_bit_input[13], _32_bit_input[14], _32_bit_input[15], _32_bit_input[16], _32_bit_input[17], _32_bit_input[18], _32_bit_input[19], _32_bit_input[20], _32_bit_input[21], _32_bit_input[22], _32_bit_input[23], _32_bit_input[24], _32_bit_input[25], _32_bit_input[26], _32_bit_input[27], _32_bit_input[28], _32_bit_input[29], _32_bit_input[30], _32_bit_input[31]}),
    .index(shift_amount), .found(bitfinder_1_found));
  // _7404 7404_1: pin names not known; wires that end beside it: bitfinder_1_found, all_zeros
  Shifter #(.width(32)) shifter_1 (.in(_32_bit_input), .\dist (shift_amount), .out(_32_bit_output));

  assign out_2 = _32_bit_input;

  // Notes on the sheet:
  //   bit position changed
  //   1 if output contains all 0's
endmodule
